# Fritzing sketch Rover PCB as Breadboard (saved by Fritzing 0.9.3b)
breadboards: 1

parts:
  U1 = L298 [package=multiwatt15_6400bgheatsink]
  Part1 = Arduino Nano (Rev3.0)
  M1 = DC Motor
  M2 = DC Motor
  hc-sr1 = hc-sr04
  hc-sr2 = hc-sr04
  R1 = Photocell (LDR) [package=THT]
  R2 = Photocell (LDR) [package=THT]
  R3 = Photocell (LDR) [package=THT]
  R4 = Resistor [tolerance=±5% resistance=10k package=THT]
  R5 = Resistor [tolerance=±5% resistance=10k package=THT]
  R6 = Resistor [tolerance=±5% resistance=10k package=THT]

nets:
  N1: U1.OUT1, M1.pin_2
  N2: U1.OUT2, M1.pin_1
  N3: U1.IN1, Part1.D12/MISO
  N4: U1.ENA, Part1.D10
  N5: U1.IN2, Part1.D11/MOSI
  N6: U1.IN3, Part1.D8
  N7: U1.ENB, Part1.D9
  N8: U1.IN4, Part1.D7
  N9: U1.OUT3, M2.pin_2
  N10: U1.OUT4, M2.pin_1
  N11: Part1.GND, R1.pin_0, R2.pin_0, R3.pin_0
  N12: Part1.D4, hc-sr2.Trig
  N13: Part1.D5, hc-sr2.Echo
  N14: Part1.5V, R4.Pin_1, R5.Pin_1, R6.Pin_1
  N15: Part1.A7, R1.pin_1, R4.Pin_0
  N16: Part1.A6, R3.pin_1, R5.Pin_0
  N17: Part1.A3, hc-sr1.Echo
  N18: Part1.A2, R2.pin_1, R6.Pin_0
  N19: Part1.D13/SCK, hc-sr1.Trig
