# Fritzing sketch Story 11 Breadboard (saved by Fritzing 0.9.3b)
breadboards: 1

parts:
  Part1 = Arduino Nano (Rev3.0)
  LED1 = LED - 5mm [color="Green (565nm)" package="5 mm [THT]"]
  LED2 = LED - 5mm [color="Yellow (585nm)" package="5 mm [THT]"]
  R1 = Resistor [tolerance=±5% resistance=100 package=THT]
  R2 = Resistor [tolerance=±5% resistance=100 package=THT]
  R3 = Resistor [tolerance=±5% resistance=100 package=THT]
  LED3 = LED - 5mm [color="Red (633nm)" package="5 mm [THT]"]
  LED4 = LED - 5mm [color="Red (633nm)" package="5 mm [THT]"]
  LED5 = LED - 5mm [color="Yellow (585nm)" package="5 mm [THT]"]
  LED6 = LED - 5mm [color="Green (565nm)" package="5 mm [THT]"]
  R4 = Resistor [tolerance=±5% resistance=100 package=THT]
  R5 = Resistor [tolerance=±5% resistance=100 package=THT]
  R6 = Resistor [tolerance=±5% resistance=100 package=THT]
  S1 = Pushbutton [package="[THT]"]
  S2 = Pushbutton [package="[THT]"]
  R7 = Resistor [tolerance=±5% resistance=10k package=THT]
  R8 = Resistor [tolerance=±5% resistance=10k package=THT]
  hc-sr1 = hc-sr04
  hc-sr2 = hc-sr04
  R9 = Resistor [tolerance=±5% resistance=10k package=THT]
  R10 = Photocell (LDR) [package=THT]
  R11 = Resistor [tolerance=±5% resistance=10k package=THT]
  R12 = Photocell (LDR) [package=THT]
  R13 = Resistor [tolerance=±5% resistance=10k package=THT]
  R14 = Photocell (LDR) [package=THT]

nets:
  GND: Part1.GND, R1.Pin_1, R2.Pin_1, R3.Pin_1, R4.Pin_1, R5.Pin_1, R6.Pin_1, S1.Pin_3, S1.Pin_4, S2.Pin_3, S2.Pin_4, hc-sr1.GND, hc-sr2.GND, R10.pin_0, R12.pin_0, R14.pin_0
  N1: Part1.D2, S1.Pin_1, S1.Pin_2, R7.Pin_0
  N2: Part1.D3, S2.Pin_1, S2.Pin_2, R8.Pin_0
  N3: Part1.D4, hc-sr1.Trig
  N4: Part1.D5, hc-sr1.Echo
  N5: Part1.D7, LED1.anode
  N6: Part1.D8, LED2.anode
  N7: Part1.D9, LED3.anode
  N8: Part1.D10, LED4.anode
  N9: Part1.D11/MOSI, LED6.anode
  N10: Part1.D12/MISO, LED5.anode
  VCC: Part1.5V, R7.Pin_1, R8.Pin_1, hc-sr1.VCC, hc-sr2.VCC, R9.Pin_1, R11.Pin_1, R13.Pin_1
  N11: Part1.A7, R9.Pin_0, R10.pin_1
  N12: Part1.A6, R11.Pin_0, R14.pin_1
  N13: Part1.A3, hc-sr2.Echo
  N14: Part1.A2, R12.pin_1, R13.Pin_0
  N15: Part1.D13/SCK, hc-sr2.Trig
  N16: LED1.cathode, R2.Pin_0
  N17: LED2.cathode, R1.Pin_0
  N18: R3.Pin_0, LED3.cathode
  N19: LED4.cathode, R6.Pin_0
  N20: LED5.cathode, R5.Pin_0
  N21: LED6.cathode, R4.Pin_0
