# Fritzing sketch Story 2 Breadboard (saved by Fritzing 0.9.3b)
breadboards: 1

parts:
  Part1 = Arduino Nano (Rev3.0)
  LED1 = LED - 5mm [color="Green (565nm)" package="5 mm [THT]"]
  LED2 = LED - 5mm [color="Yellow (585nm)" package="5 mm [THT]"]
  R1 = Resistor [tolerance=±5% resistance=220 package=THT]
  R2 = Resistor [tolerance=±5% resistance=220 package=THT]

nets:
  N1: Part1.GND, R1.Pin_1, R2.Pin_1
  N2: Part1.D7, LED1.anode
  N3: Part1.D8, LED2.anode
  N4: LED1.cathode, R2.Pin_0
  N5: LED2.cathode, R1.Pin_0
