# Fritzing sketch Story 3 Breadboard (saved by Fritzing 0.9.3b)
breadboards: 1

parts:
  Part1 = Arduino Nano (Rev3.0)
  LED1 = LED - 5mm [color="Green (565nm)" package="5 mm [THT]"]
  LED2 = LED - 5mm [color="Yellow (585nm)" package="5 mm [THT]"]
  R1 = Resistor [tolerance=±5% resistance=220 package=THT]
  R2 = Resistor [tolerance=±5% resistance=220 package=THT]
  R3 = Resistor [tolerance=±5% resistance=220 package=THT]
  LED3 = LED - 5mm [color="Red (633nm)" package="5 mm [THT]"]
  LED4 = LED - 5mm [color="Red (633nm)" package="5 mm [THT]"]
  LED5 = LED - 5mm [color="Yellow (585nm)" package="5 mm [THT]"]
  LED6 = LED - 5mm [color="Green (565nm)" package="5 mm [THT]"]
  R4 = Resistor [tolerance=±5% resistance=220 package=THT]
  R5 = Resistor [tolerance=±5% resistance=220 package=THT]
  R6 = Resistor [tolerance=±5% resistance=220 package=THT]

nets:
  N1: Part1.GND, R1.Pin_1, R2.Pin_1, R3.Pin_1, R4.Pin_1, R5.Pin_1, R6.Pin_1
  N2: Part1.D7, LED1.anode
  N3: Part1.D8, LED2.anode
  N4: Part1.D9, LED3.anode
  N5: Part1.D10, LED4.anode
  N6: Part1.D11/MOSI, LED6.anode
  N7: Part1.D12/MISO, LED5.anode
  N8: LED1.cathode, R2.Pin_0
  N9: LED2.cathode, R1.Pin_0
  N10: R3.Pin_0, LED3.cathode
  N11: LED4.cathode, R6.Pin_0
  N12: LED5.cathode, R5.Pin_0
  N13: LED6.cathode, R4.Pin_0
